// Logisim project single_cycle.circ as structural Verilog: 3 circuits, main circuit main
module main (
);

  wire and_1_out, clock_1_out, control_1_alusrc, control_1_branch, control_1_memread, control_1_memtoreg,
       control_1_memwrite, control_1_regdst, mips_alu_1_p4, registerfile_1_p3, registerfile_1_p7;
  wire [1:0] control_1_aluop;
  wire [3:0] mips_alu_1_p3;
  wire [4:0] mipsprogramrom_1_p2, mipsprogramrom_1_p2_2, mipsprogramrom_1_p2_4, multiplexer_1_out;
  wire [31:0] adder_1_out, adder_2_out, mips_alu_1_p5, mips_alu_1_p11, mipsprogramrom_1_p2_3,
       multiplexer_2_out, multiplexer_3_out, register_1_q, registerfile_1_p1, registerfile_1_p8,
       shifter_1_out;

  Register #(.width(32)) register_1 (
    .D(multiplexer_3_out), .en(1'b1), .Q(register_1_q), .clk(clock_1_out));  // open: clr
  Clock clock_1 (.out(clock_1_out));
  Adder #(.width(32)) adder_1 (.a(register_1_q), .b(32'h4), .out(adder_1_out));  // open: cin, cout
  Multiplexer #(.width(5)) multiplexer_1 (
    .in0(mipsprogramrom_1_p2), .in1(mipsprogramrom_1_p2_4), .out(multiplexer_1_out), .sel(control_1_regdst));
  // MIPSProgramROM mipsprogramrom_1: pin names not known; wires that end beside it: register_1_q, {mipsprogramrom_1_p2_3[31:26], mipsprogramrom_1_p2_2, mipsprogramrom_1_p2, mipsprogramrom_1_p2_4, mipsprogramrom_1_p2_3[10:0]}
  // RegisterFile registerfile_1: pin names not known; wires that end beside it: registerfile_1_p1, clock_1_out, registerfile_1_p3, multiplexer_1_out, mipsprogramrom_1_p2_2, mipsprogramrom_1_p2, registerfile_1_p7, registerfile_1_p8
  Control control_1 (
    .Instruction(mipsprogramrom_1_p2_3[31:26]), .RegDst(control_1_regdst), .Branch(control_1_branch),
    .MemRead(control_1_memread), .MemtoReg(control_1_memtoreg), .ALUOp(control_1_aluop),
    .MemWrite(control_1_memwrite), .ALUSrc(control_1_alusrc), .RegWrite(registerfile_1_p3));
  Shifter #(.width(32)) shifter_1 (
    .in({{16{1'b0}}, mipsprogramrom_1_p2_4, mipsprogramrom_1_p2_3[10:0]}), .\dist (5'b00010),
    .out(shifter_1_out));
  Multiplexer #(.width(32)) multiplexer_2 (
    .in0(registerfile_1_p8), .out(multiplexer_2_out), .sel(control_1_alusrc));  // open: in1
  Adder #(.width(32)) adder_2 (.a(adder_1_out), .b(shifter_1_out), .out(adder_2_out));  // open: cin, cout
  // Mips_ALU mips_alu_1: pin names not known; wires that end beside it: registerfile_1_p7, multiplexer_2_out, mips_alu_1_p3, mips_alu_1_p4, mips_alu_1_p5, mips_alu_1_p5, registerfile_1_p8, control_1_memwrite, control_1_memread, clock_1_out, mips_alu_1_p11
  ALU_control alu_control_1 (.Instruction(mipsprogramrom_1_p2_3[5:0]), .ALUop(control_1_aluop), .Output(mips_alu_1_p3));
  Multiplexer #(.width(32)) multiplexer_3 (
    .in0(adder_1_out), .in1(adder_2_out), .out(multiplexer_3_out), .sel(and_1_out));
  and and_1 (and_1_out, control_1_branch, mips_alu_1_p4);
  Multiplexer #(.width(32)) multiplexer_4 (
    .in0(mips_alu_1_p11), .in1(mips_alu_1_p5), .out(registerfile_1_p1), .sel(control_1_memtoreg));

  // Notes on the sheet:
  //   contents of mipsprogramrom_1 (hex, n*v repeats v):
  //   LABEL:     beq $t0, $t0, LABEL
  //   Hmm...?
endmodule

module Control (
  input  [5:0] Instruction,
  output RegDst,
  output Branch,
  output MemRead,
  output MemtoReg,
  output [1:0] ALUOp,
  output MemWrite,
  output ALUSrc,
  output RegWrite
);

  PLA #(.in_width(6), .out_width(9), .truth_table("000000,100010001#R-format\n100011,001100011#lw\n101011,000100110#sw\n000100,010001000#beq\n000000,000000000#\n000000,000000000#\n000000,000000000#\n000000,000000000#")) pla_1 ();  // open: in, out

  // Notes on the sheet:
  //   TODO: Implementer resterende instruktioner.
endmodule

module ALU_control (
  input  [5:0] Instruction,
  input  [1:0] ALUop,
  output [3:0] Output
);


  // Notes on the sheet:
  //   TODO: Implementer ALU control.
endmodule
